# Fritzing sketch LedBrightnessControl_BH1750 (saved by Fritzing 0.9.3b)
breadboards: 1

parts:
  R1 = Resistor [tolerance=±5% resistance=220 package="2010 [SMD]"]
  Part1 = BH1750
  LED1 = LEDs [package=led10mm]
  Part2 = Arduino Uno (Rev3)

nets:
  N1: R1.Pin_0, R1.Pin_1, LED1.A, Part2.D7
  VCC: Part1.VCC, Part2.5V
  GND: Part1.GND, LED1.C, Part2.GND
  N2: Part1.SCL, Part2.A5/SCL
  N3: Part1.SDA, Part2.A4/SDA

custom parts:
  BH1750: Light Sensor
